# Fritzing sketch wiring_esp32 (saved by Fritzing 0.9.5d)
breadboards: 1

parts:
  U1 = ESP32-38PinWide [part_number=ESP32-38PinWide]
  U2 = ESP32-38PinWide [part_number=ESP32-38PinWide]
  L298N1 = L298N DC motor driver
  MOTOR1 = 28BYJ-48 Stepper Motor
  BREAKOUT1 = ULN2003A breakout board
  HC-SR04_Sensor_1 = HC-SR04 Ultrasonic Distance Sensor
  HC-SR04_Sensor_2 = HC-SR04 Ultrasonic Distance Sensor
  HC-SR04_Sensor_3 = HC-SR04 Ultrasonic Distance Sensor
  HC-SR04_Sensor_4 = HC-SR04 Ultrasonic Distance Sensor
  M1 = DC Motor
  M2 = DC Motor
  GY-1 = GY-271 [part_number=GY-271]
  R3 = Resistor [tolerance=±5% resistance=1k package="0805 [SMD]"]
  R4 = Resistor [tolerance=±5% resistance=2.2k package="0805 [SMD]"]
  Bauteil1 = Arduino Pro Mini (5V)
  BATT1 = 3x18650 Switchable Battery Pack w/Bare Wire

nets:
  N1: U1.GPIO26, L298N1.IN4
  N2: U1.GPIO27, L298N1.IN3
  N3: U1.GPIO14, L298N1.ENB
  N4: U1.GPIO12, L298N1.IN2
  GND: U1.GND, U2.GND, L298N1.GND, BREAKOUT1.0V, HC-SR04_Sensor_1.GND, HC-SR04_Sensor_2.GND, HC-SR04_Sensor_3.GND, HC-SR04_Sensor_4.GND, GY-1.GND, R4.Pin_1, Bauteil1.GND, BATT1.NEG
  N5: U1.GPIO13, L298N1.IN1
  VIN: U1.VIN, U2.VIN, L298N1.5V, BREAKOUT1.+5V, Bauteil1.VCC
  N6: U1.GPIO15, BREAKOUT1.In_4
  N7: U1.GPIO2, BREAKOUT1.In_3
  N8: U1.GPIO0, BREAKOUT1.In_2
  N9: U1.GPIO4, BREAKOUT1.In_1
  N10: U1.GPIO16, R3.Pin_1, R4.Pin_0
  N11: U1.GPIO5, L298N1.ENA
  N12: U1.GPIO21, U2.GPIO21, GY-1.DRDY, GY-1.SDA
  N13: U1.GPIO22, U2.GPIO22, GY-1.SCL
  VCC: U2.3.3, HC-SR04_Sensor_1.VCC, HC-SR04_Sensor_2.VCC, HC-SR04_Sensor_3.VCC, HC-SR04_Sensor_4.VCC, GY-1.VCC
  N14: U2.GPIO26, HC-SR04_Sensor_3.ECHO
  N15: U2.GPIO27, HC-SR04_Sensor_3.TRIG
  N16: U2.GPIO14, HC-SR04_Sensor_4.TRIG
  N17: U2.GPIO12, HC-SR04_Sensor_4.ECHO
  N18: U2.GPIO2, HC-SR04_Sensor_2.TRIG
  N19: U2.GPIO4, HC-SR04_Sensor_2.ECHO
  N20: U2.GPIO18, HC-SR04_Sensor_1.ECHO
  N21: U2.GPIO19, HC-SR04_Sensor_1.TRIG
  N22: L298N1.OUT1, M2.pin_2
  N23: L298N1.OUT2, M2.pin_1
  N24: L298N1.OUT3, M1.pin_2
  N25: L298N1.OUT4, M1.pin_1
  N26: L298N1.12V, BATT1.POS
  N27: MOTOR1.RED, BREAKOUT1.RED_wire
  N28: MOTOR1.ORANGE, BREAKOUT1.ORANGE_wire
  N29: MOTOR1.YELLOW, BREAKOUT1.YELLOW_wire
  N30: MOTOR1.PINK, BREAKOUT1.PINK_wire
  N31: MOTOR1.BLUE, BREAKOUT1.BLUE_wire
  N32: R3.Pin_0, Bauteil1.TXO

custom parts:
  ESP32-38PinWide: Generic 38-Pin ESP32 with wide format (only access to one side of pins on a breadboard) based on Stephen Lilley's HiLetgo ESP-WROOM-32 ESP32 ESP-32S Development Board.
  L298N DC motor driver: 2x DC motor driver with 78M05 positive voltage regulator (7..35 V) L298N: max 46 V, 2 A Set 5 V Enable jumper to enable 5 V regultor (needed for the L298N) and +5 V output at screw terminal or supply external +5 V at screw terminal Set ENA and/or ENB to +5 V to enable motor permanently or supply ENA and/or ENB with PWM signal IN1 and IN2 set rotation directory for motor A (OUT1/OUT2) IN2 and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
  ULN2003A breakout board: ULN2003A 7-way Darlington Transistor Driver on breakoutboard
  GY-271: GY-271 - Electronic compass module - 3 Axis Magnetic Field Sensor HMC5883L
  3x18650 Switchable Battery Pack w/Bare Wire: 3x18650 Switchable Battery Pack w/Bare Wire Connectors
