# Fritzing sketch wiring_rpi (saved by Fritzing 0.9.5d)
breadboards: 1

parts:
  L298N1 = L298N DC motor driver
  MOTOR1 = 28BYJ-48 Stepper Motor
  BREAKOUT1 = ULN2003A breakout board
  HC-SR04_Sensor_2 = HC-SR04 Ultrasonic Distance Sensor
  M1 = DC Motor
  M2 = DC Motor
  BATT1 = 3x18650 Switchable Battery Pack w/Bare Wire
  Raspberry_Pi_1 = Raspberry Pi 3 [part_number=RPI-3-V1.2]
  PWM1 = PCA9685 16x12-bit PWM Breakout
  KIS-3R33S1 = KIS-3R33S

nets:
  N1: L298N1.OUT1, M2.pin_2
  N2: L298N1.OUT2, M2.pin_1
  N3: L298N1.OUT3, M1.pin_2
  N4: L298N1.OUT4, M1.pin_1
  N5: L298N1.12V, BATT1.POS
  GND: L298N1.GND, BREAKOUT1.0V, HC-SR04_Sensor_2.GND, BATT1.NEG, Raspberry_Pi_1.GND, PWM1.no_name_yet#601, KIS-3R33S1.IN-
  5V: L298N1.5V, BREAKOUT1.+5V
  N6: L298N1.ENA, PWM1.no_name_yet#1
  N7: L298N1.ENB, PWM1.no_name_yet#0
  N8: L298N1.IN1, Raspberry_Pi_1.GIPO27
  N9: L298N1.IN2, Raspberry_Pi_1.GIPO22
  N10: L298N1.IN3, Raspberry_Pi_1.GIPO5
  N11: L298N1.IN4, Raspberry_Pi_1.GIPO6
  N12: MOTOR1.RED, BREAKOUT1.RED_wire
  N13: MOTOR1.ORANGE, BREAKOUT1.ORANGE_wire
  N14: MOTOR1.YELLOW, BREAKOUT1.YELLOW_wire
  N15: MOTOR1.PINK, BREAKOUT1.PINK_wire
  N16: MOTOR1.BLUE, BREAKOUT1.BLUE_wire
  N17: BREAKOUT1.In_1, Raspberry_Pi_1.GIPO13
  N18: BREAKOUT1.In_2, Raspberry_Pi_1.GIPO19
  N19: BREAKOUT1.In_3, Raspberry_Pi_1.GIPO26
  N20: BREAKOUT1.In_4, Raspberry_Pi_1.GIPO16
  3V3: HC-SR04_Sensor_2.VCC, Raspberry_Pi_1.3v3, Raspberry_Pi_1.3V3, PWM1.no_name_yet#605
  N21: HC-SR04_Sensor_2.TRIG, Raspberry_Pi_1.GIPO23
  N22: HC-SR04_Sensor_2.ECHO, Raspberry_Pi_1.GIPO24
  N23: Raspberry_Pi_1.GPIO2, PWM1.no_name_yet#604
  N24: Raspberry_Pi_1.GPIO3, PWM1.no_name_yet#603
  N25: Raspberry_Pi_1.5V, KIS-3R33S1.IN+

custom parts:
  L298N DC motor driver: 2x DC motor driver with 78M05 positive voltage regulator (7..35 V) L298N: max 46 V, 2 A Set 5 V Enable jumper to enable 5 V regultor (needed for the L298N) and +5 V output at screw terminal or supply external +5 V at screw terminal Set ENA and/or ENB to +5 V to enable motor permanently or supply ENA and/or ENB with PWM signal IN1 and IN2 set rotation directory for motor A (OUT1/OUT2) IN2 and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
  ULN2003A breakout board: ULN2003A 7-way Darlington Transistor Driver on breakoutboard
  3x18650 Switchable Battery Pack w/Bare Wire: 3x18650 Switchable Battery Pack w/Bare Wire Connectors
